// Logisim project cerradura_pin.circ as structural Verilog: 3 circuits, main circuit main
module PinChecker (
  input  D,
  input  CLK,
  input  Reset,
  output Q1,
  output Q0,
  output match,
  output wrong
);

  wire D_nQ0_out, D_nQ1_Q0_out, D_Q1_nQ0_out, N1_out, not_2_out, not_3_out, undriven, undriven_2, undriven_3,
       undriven_4, undriven_5, undriven_6, undriven_7, undriven_8, undriven_9, undriven_10, undriven_11;

  not not_1 (wrong, undriven);
  not not_2 (not_2_out, Q1);
  not not_3 (not_3_out, Q0);
  and D_nQ1_Q0 (D_nQ1_Q0_out, undriven_2, not_2_out, undriven_8);
  and D_Q1_nQ0 (D_Q1_nQ0_out, undriven_3, undriven_6, undriven_9);
  and D_nQ0 (D_nQ0_out, undriven_4, not_3_out);
  and D_Q1_Q0 (match, D, undriven_5, undriven_7);
  or N1 (N1_out, D_nQ1_Q0_out, D_Q1_nQ0_out);
  D_Flip_Flop FF_Q1 (.D(N1_out), .clk(CLK), .Q(Q1), .reset(Reset));  // open: Qn, preset
  D_Flip_Flop FF_Q0 (.D(D_nQ0_out), .clk(undriven_10), .Q(Q0), .reset(undriven_11));  // open: Qn, preset

  // Notes on the sheet:
  //   D
  //   D'
  //   Q1
  //   Q1'
  //   Q0
  //   Q0'
endmodule

module LockController (
  input  match,
  input  wrong,
  input  L,
  input  CLK,
  input  Reset,
  output Q2,
  output Q1,
  output Q0,
  output unlock,
  output alarm,
  output locked
);

  wire M_nQ0_nQ2_out, M_nQ1_nQ2_out, N0_out, N1_out, N2_out, not_1_out, not_2_out, not_3_out, not_4_out,
       not_5_out, not_6_out, nQ0_nQ2_out, nQ1_nQ2_out, Q0_nM_nW_out, Q0_W_out, Q1_nM_out, Q1_Q0_out,
       Q2_nL_out, undriven, undriven_2, undriven_3, undriven_4, undriven_5, undriven_6, undriven_7,
       undriven_8, undriven_9, undriven_10, undriven_11, undriven_12, undriven_13, undriven_14, undriven_15,
       undriven_16, undriven_17, undriven_18, undriven_19, undriven_20, undriven_21, undriven_22,
       undriven_23, undriven_24, W_nQ0_nQ2_out;

  not not_1 (not_1_out, undriven);
  not not_2 (not_2_out, undriven_2);
  not not_3 (not_3_out, undriven_3);
  not not_4 (not_4_out, Q2);
  not not_5 (not_5_out, Q1);
  not not_6 (not_6_out, Q0);
  and Q2_nL (Q2_nL_out, undriven_7, not_3_out);
  and M_nQ0_nQ2 (M_nQ0_nQ2_out, undriven_4, undriven_18, undriven_8);
  and M_nQ1_nQ2 (M_nQ1_nQ2_out, match, undriven_14, undriven_9);
  and Q1_Q0 (Q1_Q0_out, undriven_13, undriven_16);
  and Q0_W (Q0_W_out, undriven_17, undriven_6);
  and Q1_nM (Q1_nM_out, undriven_12, undriven_5);
  and Q0_nM_nW (Q0_nM_nW_out, undriven_15, not_1_out, not_2_out);
  and W_nQ0_nQ2 (W_nQ0_nQ2_out, wrong, undriven_19, undriven_10);
  and nQ0_nQ2 (nQ0_nQ2_out, not_6_out, undriven_11);
  and nQ1_nQ2 (nQ1_nQ2_out, not_5_out, not_4_out);
  or N2 (N2_out, Q2_nL_out, M_nQ0_nQ2_out, M_nQ1_nQ2_out);
  or N1 (N1_out, alarm, Q0_W_out, Q1_nM_out);
  or N0 (N0_out, undriven_20, Q0_nM_nW_out, W_nQ0_nQ2_out);
  or OR_locked (locked, nQ0_nQ2_out, nQ1_nQ2_out);
  D_Flip_Flop FF_Q2 (.D(N2_out), .clk(CLK), .Q(Q2), .reset(Reset));  // open: Qn, preset
  D_Flip_Flop FF_Q1 (.D(N1_out), .clk(undriven_21), .Q(Q1), .reset(undriven_23));  // open: Qn, preset
  D_Flip_Flop FF_Q0 (.D(N0_out), .clk(undriven_22), .Q(Q0), .reset(undriven_24));  // open: Qn, preset

  // Notes on the sheet:
  //   match
  //   match'
  //   wrong
  //   wrong'
  //   L
  //   L'
  //   Q2
  //   Q2'
  //   Q1
  //   Q1'
  //   Q0
  //   Q0'
endmodule

module main (
  input  D,
  input  L,
  input  Reset,
  input  CLK,
  output match,
  output wrong,
  output unlock,
  output alarm,
  output locked
);

  wire lockcontroller_1_p1, lockcontroller_1_p2;

  // PinChecker pinchecker_1: pin names not known; wires that end beside it: D, CLK, Reset, match, wrong
  // LockController lockcontroller_1: pin names not known; wires that end beside it: lockcontroller_1_p1, lockcontroller_1_p2, L, CLK, Reset, unlock, alarm, locked
endmodule
